# Fritzing sketch mcp3008 (saved by Fritzing 0.9.5d)
breadboards: 1

parts:
  ADC1 = MCP3008 [package=dil16]
  Mod1 = Raspberry Pi Pico
  R1 = Resistor [tolerance=±5% resistance=10k package="0603 [SMD]"]
  R3 = Resistor [tolerance=±5% resistance=10k package="0603 [SMD]"]
  R4 = Resistor [tolerance=±5% resistance=10k package="0603 [SMD]"]
  R5 = Resistor [tolerance=±5% resistance=1k package="0603 [SMD]"]

nets:
  N1: ADC1.CH0, R1.Pin_1, R4.Pin_0
  N2: ADC1.CH1, R3.Pin_1, R5.Pin_0
  N3: ADC1.CH2, ADC1.CH3, ADC1.CH4, ADC1.CH5, ADC1.CH6, ADC1.CH7, ADC1.DGND, ADC1.AGND, Mod1.pin_3, Mod1.pin_8, Mod1.pin_13, Mod1.pin_18, Mod1.pin_23, Mod1.pin_28, Mod1.pin_33, Mod1.pin_38, R4.Pin_1, R5.Pin_1
  N4: ADC1.CS/SHDN, Mod1.pin_22
  N5: ADC1.Din, Mod1.pin_25
  N6: ADC1.Dout, Mod1.pin_21
  N7: ADC1.CLK, Mod1.pin_24
  N8: ADC1.VREF, ADC1.VDD, Mod1.pin_36, R1.Pin_0, R3.Pin_0

custom parts:
  Raspberry Pi Pico: Raspberry Pi Pico. Based around the RP2040 microcontroller the Pico is a low cost microcontroller device bringing Raspberry Pi quality, cost, and easy of use to the microcontroller space. Jan 2021, Split part in to two versions: tht (this one) and SMD. This one will drill holes for a .1 in header in pcb to allow plugging in the module as well as providing pads to solder the module to the top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
